# Fritzing sketch fritzing (saved by Fritzing 0.9.3b)
breadboards: 1

parts:
  Part1 = Barometric Pressure Sensor - BMP180 Breakout (GY-68)
  Part3 = Arduino Nano 33 BLE Sense
  OLED1 = OLED 128x64 I2C Monochrome Display VDD-GND
  S1 = Momentary Switch [package=ksa_sealed_tac_switch]
  LED1 = Green LED - Rect 5x2x7mm [package="5x2x7 mm [THT]"]
  R1 = Resistor [tolerance=±5% resistance=220 package=THT]
  R2 = Resistor [tolerance=±5% resistance=220 package=THT]
  U1 = ATTINY45 [package=so]
  BAT1 = BC9VPC [package=bc9vpc]
  U2 = LM2931 [package=so08]

nets:
  VCC: Part1.VCC, Part3.3V3, OLED1.VDD, U1.PB5(NRES)
  GND: Part1.GND, Part3.GND, Part3.A7, OLED1.GND, S1.2, LED1.cathode, R1.Pin_0, R2.Pin_1, U1.PB3(ADC3), BAT1.V-, U2.GND
  N1: Part1.SCL, Part3.A5, OLED1.SCK, U1.PB4(ADC2)
  N2: Part1.SDA, Part3.A4, OLED1.SDA, U1.GND
  N3: Part3.D2, LED1.anode
  N4: Part3.D3~, S1.3
  N5: Part3.D11/MOSI, Part3.+5V
  N6: Part3.A0, R1.Pin_1, R2.Pin_0
  N7: BAT1.V+, U2.OUT

notes:
  DFRobot IIC Ozone Sensor
  DFRobot Anemometer Kit
  3K3
  2K2

custom parts:
  Arduino Nano 33 BLE Sense: The Nano 33 BLE Sense (without headers) is Arduino’s 3.3V AI enabled board in the smallest available form factor: 45x18mm! The Arduino Nano 33 BLE Sense is a completely new board on a well-known form factor. It comes with a series of embedded sensors: 9 axis inertial sensor: what makes this board ideal for wearable devices humidity, and temperature sensor: to get highly accurate measurements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
  OLED 128x64 I2C Monochrome Display VDD-GND: OLED 128x64 I2C Monochrome Display. Note: there are two variants of this part, this one is the VDD GND SCK SDA variant. The other is GND VDD SCK SDA. Make sure you select the part that matches your module as using the incorrect part will probably destroy your module! In addition the mounting holes are marked on silkscreen but not by default drilled. If you want drilled mounting holes, copy a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
  Green LED - Rect 5x2x7mm: A generic rectangular green LED (~1.8V) 5mm x 2mm x 7mm
